// Logisim project test_circuit_emu.circ as structural Verilog: 1 circuit, main circuit main
module main (
  output [15:0] r0,
  output [15:0] r1,
  output [15:0] r2,
  output [15:0] r3,
  output [15:0] r4,
  output [15:0] r5,
  output [15:0] r6,
  output [15:0] r7,
  output [15:0] fp,
  output [15:0] pc,
  output [15:0] sp,
  output [15:0] ps,
  output halt
);

  wire cdm_16_1_p14, cdm_16_1_p15, cdm_16_1_p16, cdm_16_1_p17, clock_1_out, not_1_out;
  wire [1:0] cdm_16_1_p7;
  wire [15:0] cdm_16_1_p18, cdm_16_1_p19, controlled_buffer_1_out;

  Clock clock_1 (.out(clock_1_out));
  // CdM_16 cdm_16_1: pin names not known; wires that end beside it: r0, r1, clock_1_out, r2, r3, r4, cdm_16_1_p7, r5, r6, fp, pc, sp, ps, cdm_16_1_p14, cdm_16_1_p15, cdm_16_1_p16, cdm_16_1_p17, cdm_16_1_p18, cdm_16_1_p19
  Decoder #(.select(2), .enable("false")) decoder_1 (.out2(halt), .sel(cdm_16_1_p7));  // open: out0, out1, out3
  not not_1 (not_1_out, cdm_16_1_p15);
  assign controlled_buffer_1_out = not_1_out ? cdm_16_1_p18 : 16'bz;  // Controlled_Buffer controlled_buffer_1
  assign cdm_16_1_p19 = cdm_16_1_p15 ? controlled_buffer_1_out : 16'bz;  // Controlled_Buffer controlled_buffer_2
  // RAM ram_1: pin names not known; wires that end beside it: cdm_16_1_p17, cdm_16_1_p16, cdm_16_1_p14, clock_1_out, cdm_16_1_p15, controlled_buffer_1_out

  assign r7 = fp;
endmodule
